// Digital circuit 1-bit Adder Circuit.dig as structural Verilog
module _1_bit_Adder_Circuit (
  input  A,
  input  B,
  input  Cin,
  output S,
  output Cout
);

  wire and_1_out, and_2_out, xor_1_out;

  xor xor_1 (xor_1_out, A, B);
  and and_1 (and_1_out, xor_1_out, Cin);
  and and_2 (and_2_out, B, A);
  xor xor_2 (S, xor_1_out, Cin);
  or or_1 (Cout, and_1_out, and_2_out);
  LED led_1 (.in(S));
  LED led_2 (.in(Cout));
endmodule
