// Digital circuit 4-bit Adder Program.dig as structural Verilog
module _4_bit_Adder_Program (
  input  [3:0] A,
  input  [3:0] B,
  output [3:0] Sum,
  output Overflow
);

  wire _1_bit_adder_circuit_2_cout, _1_bit_adder_circuit_3_cout, _1_bit_adder_circuit_4_cout;

  _1_bit_Adder_Circuit _1_bit_adder_circuit_1 (
    .A(A[3]), .B(B[3]), .Cin(_1_bit_adder_circuit_2_cout), .S(Sum[3]), .Cout(Overflow));
  _1_bit_Adder_Circuit _1_bit_adder_circuit_2 (
    .A(A[2]), .B(B[2]), .Cin(_1_bit_adder_circuit_3_cout), .S(Sum[2]), .Cout(_1_bit_adder_circuit_2_cout));
  _1_bit_Adder_Circuit _1_bit_adder_circuit_3 (
    .A(A[1]), .B(B[1]), .Cin(_1_bit_adder_circuit_4_cout), .S(Sum[1]), .Cout(_1_bit_adder_circuit_3_cout));
  _1_bit_Adder_Circuit _1_bit_adder_circuit_4 (
    .A(A[0]), .B(B[0]), .Cin(1'b0), .S(Sum[0]), .Cout(_1_bit_adder_circuit_4_cout));
endmodule
