// Digital circuit DRAM.dig as structural Verilog
module DRAM (
  input  nOE,
  input  nRW,
  input  nCS,
  input  [3:0] Address,
  output [3:0] Data
);

  RAMSinglePortSel #(.AddrBits(4), .Bits(4)) ramsingleportsel (.A(Address), .CS(nCS), .WE(nOE), .OE(nRW), .D(Data));
  // Pins of 1 and 4 bits meet at Data

  // Notes on the sheet:
  //   nOE: default 1
  //   nRW: default 1
  //   nCS: default 1
endmodule
