// Digital circuit GPR.dig as structural Verilog
module GPR (
  input  CLK,
  input  LD,
  input  ST,
  input  [3:0] D,
  input  CLR,
  input  [1:0] Sel_Reg,
  input  [1:0] Sel_Register,
  output [3:0] READ,
  output [3:0] Stored_Value
);

  wire and_1_out, and_2_out, and_3_out, and_4_out, and_5_out, decoder_1_out_0, decoder_1_out_1,
       decoder_1_out_2, decoder_1_out_3, demultiplexer_1_out_0, demultiplexer_1_out_1, demultiplexer_1_out_2,
       demultiplexer_1_out_3;
  wire [3:0] R0_out, R1_out, R2_out, R3_out;

  Decoder #(.Selector_Bits(2)) decoder_1 (
    .sel(Sel_Reg), .out_0(decoder_1_out_0), .out_1(decoder_1_out_1), .out_2(decoder_1_out_2),
    .out_3(decoder_1_out_3));
  Demultiplexer #(.Selector_Bits(2)) demultiplexer_1 (
    .sel(Sel_Reg), .in(ST), .out_0(demultiplexer_1_out_0), .out_1(demultiplexer_1_out_1),
    .out_2(demultiplexer_1_out_2), .out_3(demultiplexer_1_out_3));
  and and_1 (and_1_out, CLK, ST);
  and and_2 (and_2_out, LD, decoder_1_out_0);
  and and_3 (and_3_out, LD, decoder_1_out_1);
  and and_4 (and_4_out, LD, decoder_1_out_2);
  and and_5 (and_5_out, LD, decoder_1_out_3);
  _4_bit_Register R0 (.LD(and_2_out), .CLK(and_1_out), .D(D), .ST(demultiplexer_1_out_0), .CLR(CLR), .out(R0_out));
  _4_bit_Register R1 (.LD(and_3_out), .CLK(and_1_out), .D(D), .ST(demultiplexer_1_out_1), .CLR(CLR), .out(R1_out));
  _4_bit_Register R2 (.LD(and_4_out), .CLK(and_1_out), .D(D), .ST(demultiplexer_1_out_2), .CLR(CLR), .out(R2_out));
  _4_bit_Register R3 (.LD(and_5_out), .CLK(and_1_out), .D(D), .ST(demultiplexer_1_out_3), .CLR(CLR), .out(R3_out));
  Multiplexer #(.Selector_Bits(2), .Bits(4)) multiplexer_1 (
    .sel(Sel_Reg), .in_0(R0_out), .in_1(R1_out), .in_2(R2_out), .in_3(R3_out), .out(READ));
  Multiplexer #(.Selector_Bits(2), .Bits(4)) multiplexer_2 (
    .sel(Sel_Register), .in_0(R0_out), .in_1(R1_out), .in_2(R2_out), .in_3(R3_out), .out(Stored_Value));
endmodule
