// Digital circuit IR.dig as structural Verilog
module IR (
  input  CLK,
  input  RST,
  input  [3:0] Manual,
  input  [3:0] DRAM_output,
  input  Sel_Data,
  input  Sel_Manual,
  input  LD,
  input  ST,
  output [3:0] IR_out
);

  wire [3:0] _4_bit_register_1_out, multiplexer_1_out, multiplexer_2_out;

  Multiplexer #(.Bits(4)) multiplexer_1 (.sel(Sel_Manual), .in_0(DRAM_output), .in_1(Manual), .out(multiplexer_1_out));
  Multiplexer #(.Bits(4)) multiplexer_2 (
    .sel(Sel_Data), .in_0(_4_bit_register_1_out), .in_1(multiplexer_1_out), .out(multiplexer_2_out));
  _4_bit_Register _4_bit_register_1 (
    .LD(LD), .CLK(CLK), .D(multiplexer_2_out), .ST(ST), .CLR(RST), .out(_4_bit_register_1_out));
  assign IR_out = LD ? _4_bit_register_1_out : 4'bz;  // Driver driver_1
endmodule
