// Digital circuit Registers DRAM.dig as structural Verilog
module Registers_DRAM (
  input  nOE,
  input  nRW,
  input  nCS,
  input  [3:0] Data,
  input  CLK,
  input  Sel_Manual_Data_IR,
  input  IR_ST,
  input  RST,
  input  [3:0] IR_Manual_Data,
  input  [3:0] PC_Manual_Address,
  input  Sel_GPR,
  input  [1:0] Sel_LD_Reg,
  input  GPR_LD,
  input  INC,
  input  Sel_Data_IR,
  input  IR_LD,
  input  GPR_ST,
  input  GPR_RST,
  input  Sel_Manual_PC,
  input  RST_PC,
  output [3:0] DRAM_output,
  output [3:0] IR_output,
  output [3:0] GPR_Input
);

  wire [3:0] gpr_1_p7, multiplexer_1_out, pc_1_pc_plus_1;

  PC pc_1 (
    .INC(INC), .Manual_Address(PC_Manual_Address), .CLK(CLK), .RST(RST_PC), .LD(Sel_Manual_PC),
    .PC_plus_1(pc_1_pc_plus_1));
  Multiplexer #(.Bits(4)) multiplexer_1 (
    .sel(Sel_GPR), .in_0(pc_1_pc_plus_1), .in_1(gpr_1_p7), .out(multiplexer_1_out));
  // DRAM dram_1: pin names not known; wires that end beside it: nOE, nRW, nCS, multiplexer_1_out, Data
  // GPR gpr_1: pin names not known; wires that end beside it: CLK, GPR_LD, GPR_ST, GPR_Input, GPR_RST, Sel_LD_Reg, gpr_1_p7
  assign DRAM_output = IR_ST ? Data : 4'bz;  // Driver driver_1
  assign GPR_Input = GPR_ST ? Data : 4'bz;  // Driver driver_2
  IR ir_1 (
    .CLK(CLK), .RST(RST), .Manual(IR_Manual_Data), .DRAM_output(DRAM_output), .Sel_Data(Sel_Data_IR),
    .Sel_Manual(Sel_Manual_Data_IR), .LD(IR_LD), .ST(IR_ST), .IR_out(IR_output));

  // Notes on the sheet:
  //   nOE: default 1
  //   nRW: default 1
  //   nCS: default 1
  //   Tri-State Buffer
endmodule
